// Logisim project saruwatari.circ as structural Verilog: 7 circuits, main circuit main
module main (
  input  reset
);

  wire alu_1_data_ready, alu_2_data_ready, clock_1_out, comparator_1_eq, control_unit_1_branch_taken,
       control_unit_1_jal, control_unit_1_jump, hazard_detection_unit_1_exmem_wb_enable,
       hazard_detection_unit_1_id_exmem_enable, hazard_detection_unit_1_id_exmem_flush,
       hazard_detection_unit_1_if_id_enable, hazard_detection_unit_1_if_id_flush,
       hazard_detection_unit_1_pc_enable, not_1_out, not_2_out, or_1_out, or_2_out, or_3_out;
  wire [3:0] alu_controller_1_out_3, alu_controller_2_out_3, EXMEM_WB_CONTROL_q;
  wire [4:0] EXMEM_WB_reg_dst_0_q, EXMEM_WB_reg_dst_1_q, multiplexer_5_out, multiplexer_6_out,
       multiplexer_8_out;
  wire [5:0] ID_EXMEM_ir_1_q_3;
  wire [9:0] control_unit_1_out_4, ID_EXMEM_CONTROL_q;
  wire [10:0] ID_EXMEM_ir_1_q;
  wire [14:0] ID_EXMEM_ir_1_q_2;
  wire [31:0] adder_1_out, adder_2_out, EXMEM_WB_alu_out_0_q, EXMEM_WB_alu_out_1_q, EXMEM_WB_LMD_q,
       EXMEM_WB_npc_q, ID_EXMEM_A0_q, ID_EXMEM_A1_q, ID_EXMEM_B0_q, ID_EXMEM_B1_q, ID_EXMEM_imm_0_q,
       ID_EXMEM_imm_1_q, ID_EXMEM_ir_0_q, ID_EXMEM_npc_q, IF_ID_ir_0_q, IF_ID_ir_1_q, IF_ID_npc_q,
       multiplexer_1_out, multiplexer_2_out, multiplexer_3_out, multiplexer_4_out, multiplexer_7_out,
       multiplexer_9_out, Program_Counter_q, ram_1_data, register_file_1_a0, register_file_1_a1,
       register_file_1_b0, register_file_1_b1, rom_1_data, sign_extensor_1_data_output,
       sign_extensor_2_data_output, undriven;

  Clock #(.highDuration(1), .lowDuration(1)) clock_1 (.out(clock_1_out));
  Register #(.width(32), .trigger("rising")) Program_Counter (
    .D(multiplexer_1_out), .en(hazard_detection_unit_1_pc_enable), .Q(Program_Counter_q), .clk(clock_1_out),
    .clr(reset));
  Adder #(.width(32)) adder_1 (.a(32'h8), .b(Program_Counter_q), .out(adder_1_out));  // open: cin, cout
  ROM #(.addrWidth(32), .dataWidth(32)) rom_1 (.addr(Program_Counter_q), .data(rom_1_data), .sel(1'b0));
  Multiplexer #(.select(1), .width(32)) multiplexer_1 (
    .in0(multiplexer_2_out), .in1(adder_1_out), .out(multiplexer_1_out), .sel(or_2_out));
  or or_1 (or_1_out, reset, hazard_detection_unit_1_if_id_flush);
  Register #(.width(32), .trigger("rising")) IF_ID_npc (
    .D(multiplexer_1_out), .en(hazard_detection_unit_1_if_id_enable), .Q(IF_ID_npc_q), .clk(clock_1_out),
    .clr(or_1_out));
  Register #(.width(32), .trigger("rising")) IF_ID_ir_1 (
    .D(rom_1_data), .en(hazard_detection_unit_1_if_id_enable), .Q(IF_ID_ir_1_q), .clk(clock_1_out),
    .clr(or_1_out));
  Register #(.width(32), .trigger("rising")) IF_ID_ir_0 (
    .D(rom_1_data), .en(hazard_detection_unit_1_if_id_enable), .Q(IF_ID_ir_0_q), .clk(clock_1_out),
    .clr(or_1_out));
  Hazard_detection_unit hazard_detection_unit_1 (
    .if_id_ir1(IF_ID_ir_1_q), .if_id_ir_0(IF_ID_ir_0_q),
    .id_exmem_ir1({ID_EXMEM_ir_1_q_3, ID_EXMEM_ir_1_q_2, ID_EXMEM_ir_1_q}), .id_exmem_ir_0(ID_EXMEM_ir_0_q),
    .alu_1_data_ready(alu_1_data_ready), .alu_0_data_ready(alu_2_data_ready),
    .jump_or_branch_taken(or_2_out), .if_id_flush(hazard_detection_unit_1_if_id_flush),
    .if_id_enable(hazard_detection_unit_1_if_id_enable), .pc_enable(hazard_detection_unit_1_pc_enable),
    .id_exmem_flush(hazard_detection_unit_1_id_exmem_flush),
    .id_exmem_enable(hazard_detection_unit_1_id_exmem_enable),
    .exmem_wb_enable(hazard_detection_unit_1_exmem_wb_enable), .clock(clock_1_out), .reset(reset));
  or or_2 (or_2_out, control_unit_1_branch_taken, control_unit_1_jump, control_unit_1_jal);
  Sign_Extensor sign_extensor_1 (.data_input(IF_ID_ir_1_q[31:16]), .data_output(sign_extensor_1_data_output));
  Sign_Extensor sign_extensor_2 (.data_input(IF_ID_ir_0_q[31:16]), .data_output(sign_extensor_2_data_output));
  Control_Unit control_unit_1 (
    .ir_1(IF_ID_ir_0_q), .ir_0(IF_ID_ir_1_q), .branch_operand_is_zero(comparator_1_eq),
    .branch_taken(control_unit_1_branch_taken), .jump(control_unit_1_jump), .jal(control_unit_1_jal),
    .out_4(control_unit_1_out_4));
  not not_1 (not_1_out, clock_1_out);
  Adder #(.width(32)) adder_2 (.a(IF_ID_npc_q), .b(sign_extensor_1_data_output), .out(adder_2_out));  // open: cin, cout
  Register_File register_file_1 (
    .read_11(IF_ID_ir_1_q[15:11]), .read_12(IF_ID_ir_1_q[10:6]), .read_01(IF_ID_ir_0_q[15:11]),
    .read_02(IF_ID_ir_0_q[10:6]), .clock(not_1_out), .reset(reset),
    .reg_file_write_enable_1(EXMEM_WB_CONTROL_q[0]), .reg_file_write_address_1(multiplexer_8_out),
    .reg_file_data_1(multiplexer_7_out), .reg_file_write_enable_0(EXMEM_WB_CONTROL_q[3]),
    .reg_file_write_address_0(EXMEM_WB_reg_dst_0_q), .reg_file_data_0(multiplexer_9_out),
    .A1(register_file_1_a1), .B1(register_file_1_b1), .A0(register_file_1_a0), .B0(register_file_1_b0));
  Multiplexer #(.select(1), .width(32)) multiplexer_2 (
    .in0(register_file_1_a1), .in1(adder_2_out), .out(multiplexer_2_out), .sel(or_2_out));
  Comparator #(.width(32), .mode("unsigned")) comparator_1 (
    .a(register_file_1_a1), .b({32{1'b0}}), .eq(comparator_1_eq));  // open: gt, lt
  or or_3 (or_3_out, hazard_detection_unit_1_id_exmem_flush, reset);
  Register #(.width(32), .trigger("rising")) ID_EXMEM_npc (
    .D(IF_ID_npc_q), .en(hazard_detection_unit_1_id_exmem_enable), .Q(ID_EXMEM_npc_q), .clk(clock_1_out),
    .clr(or_3_out));
  Register #(.width(32), .trigger("rising")) ID_EXMEM_ir_1 (
    .D(IF_ID_ir_1_q), .en(hazard_detection_unit_1_id_exmem_enable),
    .Q({ID_EXMEM_ir_1_q_3, ID_EXMEM_ir_1_q_2, ID_EXMEM_ir_1_q}), .clk(clock_1_out), .clr(or_3_out));
  Register #(.width(32), .trigger("rising")) ID_EXMEM_ir_0 (
    .D(IF_ID_ir_0_q), .en(hazard_detection_unit_1_id_exmem_enable), .Q(ID_EXMEM_ir_0_q), .clk(clock_1_out),
    .clr(or_3_out));
  Register #(.width(32), .trigger("rising")) ID_EXMEM_imm_1 (
    .D(sign_extensor_1_data_output), .en(hazard_detection_unit_1_id_exmem_enable), .Q(ID_EXMEM_imm_1_q),
    .clk(clock_1_out), .clr(or_3_out));
  Register #(.width(32), .trigger("rising")) ID_EXMEM_imm_0 (
    .D(sign_extensor_2_data_output), .en(hazard_detection_unit_1_id_exmem_enable), .Q(ID_EXMEM_imm_0_q),
    .clk(clock_1_out), .clr(or_3_out));
  Register #(.width(32), .trigger("rising")) ID_EXMEM_A1 (
    .D(register_file_1_a1), .en(hazard_detection_unit_1_id_exmem_enable), .Q(ID_EXMEM_A1_q),
    .clk(clock_1_out), .clr(or_3_out));
  Register #(.width(32), .trigger("rising")) ID_EXMEM_B1 (
    .D(register_file_1_b1), .en(hazard_detection_unit_1_id_exmem_enable), .Q(ID_EXMEM_B1_q),
    .clk(clock_1_out), .clr(or_3_out));
  Register #(.width(32), .trigger("rising")) ID_EXMEM_A0 (
    .D(register_file_1_a0), .en(hazard_detection_unit_1_id_exmem_enable), .Q(ID_EXMEM_A0_q),
    .clk(clock_1_out), .clr(or_3_out));
  Register #(.width(32), .trigger("rising")) ID_EXMEM_B0 (
    .D(register_file_1_b0), .en(hazard_detection_unit_1_id_exmem_enable), .Q(ID_EXMEM_B0_q),
    .clk(clock_1_out), .clr(or_3_out));
  Register #(.width(10), .trigger("rising")) ID_EXMEM_CONTROL (
    .D(control_unit_1_out_4), .en(hazard_detection_unit_1_id_exmem_enable), .Q(ID_EXMEM_CONTROL_q),
    .clk(clock_1_out), .clr(or_3_out));
  Multiplexer #(.select(1), .width(32)) multiplexer_3 (
    .in0(ID_EXMEM_B1_q), .in1(ID_EXMEM_imm_1_q), .out(multiplexer_3_out), .sel(ID_EXMEM_CONTROL_q[1]));
  Multiplexer #(.select(1), .width(32)) multiplexer_4 (
    .in0(ID_EXMEM_imm_0_q), .in1(ID_EXMEM_B0_q), .out(multiplexer_4_out), .sel(ID_EXMEM_CONTROL_q[0]));
  Alu alu_1 (
    .a(ID_EXMEM_A1_q), .b(multiplexer_3_out), .op(alu_controller_1_out_3), .data_ready(alu_1_data_ready),
    .alu_output(undriven));
  Alu alu_2 (
    .a(ID_EXMEM_A0_q), .b(multiplexer_4_out), .op(alu_controller_2_out_3), .data_ready(alu_2_data_ready),
    .alu_output(ram_1_data));
  Alu_Controller alu_controller_1 (.out_3(alu_controller_1_out_3), .in_1(ID_EXMEM_ir_1_q_3), .in_2(ID_EXMEM_ir_1_q));
  Alu_Controller alu_controller_2 (
    .out_3(alu_controller_2_out_3), .in_1(ID_EXMEM_ir_0_q[31:26]), .in_2(ID_EXMEM_ir_0_q[10:0]));
  not not_2 (not_2_out, clock_1_out);
  Multiplexer #(.select(1), .width(5)) multiplexer_5 (
    .in0(ID_EXMEM_ir_1_q_2[4:0]), .in1(ID_EXMEM_ir_1_q_2[9:5]), .out(multiplexer_5_out),
    .sel(ID_EXMEM_CONTROL_q[2]));
  Multiplexer #(.select(1), .width(5)) multiplexer_6 (
    .in0(ID_EXMEM_ir_0_q[15:11]), .in1(ID_EXMEM_ir_0_q[25:21]), .out(multiplexer_6_out),
    .sel(ID_EXMEM_CONTROL_q[3]));
  RAM #(.addrWidth(32), .dataWidth(32), .bus("combined")) ram_1 (
    .addr(ID_EXMEM_B0_q), .data(ram_1_data), .sel(1'b0), .clk(not_2_out), .ld(1'b1), .clr(reset));
  Register #(.width(32), .trigger("rising")) EXMEM_WB_npc (
    .D(ID_EXMEM_npc_q), .en(hazard_detection_unit_1_exmem_wb_enable), .Q(EXMEM_WB_npc_q), .clk(clock_1_out),
    .clr(reset));
  Register #(.width(5), .trigger("rising")) EXMEM_WB_reg_dst_1 (
    .D(multiplexer_5_out), .en(hazard_detection_unit_1_exmem_wb_enable), .Q(EXMEM_WB_reg_dst_1_q),
    .clk(clock_1_out), .clr(reset));
  Register #(.width(5), .trigger("rising")) EXMEM_WB_reg_dst_0 (
    .D(multiplexer_6_out), .en(hazard_detection_unit_1_exmem_wb_enable), .Q(EXMEM_WB_reg_dst_0_q),
    .clk(clock_1_out), .clr(reset));
  Register #(.width(32), .trigger("rising")) EXMEM_WB_alu_out_1 (
    .D(undriven), .en(hazard_detection_unit_1_exmem_wb_enable), .Q(EXMEM_WB_alu_out_1_q), .clk(clock_1_out),
    .clr(reset));
  Register #(.width(32), .trigger("rising")) EXMEM_WB_alu_out_0 (
    .D(ram_1_data), .en(hazard_detection_unit_1_exmem_wb_enable), .Q(EXMEM_WB_alu_out_0_q),
    .clk(clock_1_out), .clr(reset));
  Register #(.width(32), .trigger("rising")) EXMEM_WB_LMD (
    .D(ram_1_data), .en(hazard_detection_unit_1_exmem_wb_enable), .Q(EXMEM_WB_LMD_q), .clk(clock_1_out),
    .clr(reset));
  Register #(.width(4), .trigger("rising")) EXMEM_WB_CONTROL (
    .D(ID_EXMEM_CONTROL_q[9:6]), .en(hazard_detection_unit_1_exmem_wb_enable), .Q(EXMEM_WB_CONTROL_q),
    .clk(clock_1_out), .clr(reset));
  Multiplexer #(.select(1), .width(32)) multiplexer_7 (
    .in0(EXMEM_WB_npc_q), .in1(EXMEM_WB_alu_out_1_q), .out(multiplexer_7_out), .sel(EXMEM_WB_CONTROL_q[1]));
  Multiplexer #(.select(1), .width(5)) multiplexer_8 (
    .in0(EXMEM_WB_reg_dst_1_q), .in1({5{1'b1}}), .out(multiplexer_8_out), .sel(EXMEM_WB_CONTROL_q[1]));
  Multiplexer #(.select(1), .width(32)) multiplexer_9 (
    .in0(EXMEM_WB_alu_out_0_q), .in1(EXMEM_WB_LMD_q), .out(multiplexer_9_out), .sel(EXMEM_WB_CONTROL_q[2]));

  // Notes on the sheet:
  //   clock
  //   adder_8_op
  //   Instruction Memory (IM)
  //   instruction_1
  //   instruction_0
  //   address_after_jump_or_branch
  //   HDU
  //   Control Unit
  //   Sign Extensor 1
  //   Sign Extensor 0
  //   Register File
  //   ALU_1
  //   ALU_0
  //   alu_controller_1
  //   alu_controller_0
  //   Data Memory (DM)
endmodule

module Sign_Extensor (
  input  [15:0] data_input,
  output [31:0] data_output
);


  assign data_output = {{16{1'b0}}, data_input};
endmodule

module Register_File (
  input  [4:0] read_11,
  input  [4:0] read_12,
  input  [4:0] read_01,
  input  [4:0] read_02,
  input  clock,
  input  reset,
  input  reg_file_write_enable_0,
  input  reg_file_write_enable_1,
  input  [4:0] reg_file_write_address_0,
  input  [4:0] reg_file_write_address_1,
  input  [31:0] reg_file_data_0,
  input  [31:0] reg_file_data_1,
  output [31:0] A1,
  output [31:0] B1,
  output [31:0] A0,
  output [31:0] B0
);

  Register #(.width(32), .trigger("rising")) register_1 (.Q(A1), .clk(clock), .clr(reset));  // open: D, en
  Register #(.width(32), .trigger("rising")) register_2 (.Q(B1), .clk(clock), .clr(reset));  // open: D, en
  Register #(.width(32), .trigger("rising")) register_3 (.Q(A0), .clk(clock), .clr(reset));  // open: D, en
  Register #(.width(32), .trigger("rising")) register_4 (.Q(B0), .clk(clock), .clr(reset));  // open: D, en
endmodule

module Control_Unit (
  input  branch_operand_is_zero,
  input  [31:0] ir_1,
  input  [31:0] ir_0,
  output [9:0] out_4,
  output branch_taken,
  output jump,
  output jal
);
endmodule

module Alu_Controller (
  input  [5:0] in_1,
  input  [10:0] in_2,
  output [3:0] out_3
);
endmodule

module Alu (
  input  [31:0] a,
  input  [31:0] alu_output,
  input  [31:0] b,
  input  [3:0] op,
  output data_ready
);
endmodule

module Hazard_detection_unit (
  input  alu_1_data_ready,
  input  alu_0_data_ready,
  input  jump_or_branch_taken,
  input  [31:0] if_id_ir1,
  input  [31:0] if_id_ir_0,
  input  [31:0] id_exmem_ir1,
  input  [31:0] id_exmem_ir_0,
  output if_id_flush,
  output if_id_enable,
  output clock,
  output pc_enable,
  output reset,
  output id_exmem_flush,
  output id_exmem_enable,
  output exmem_wb_enable
);
endmodule
